# Fritzing sketch sensor de luminosidade (saved by Fritzing 0.9.2b)
breadboards: 1

parts:
  KY-1 = Keyes Relay [package=THT]
  e-radionica_com1 = LM393 LDR breakout [part_number=100027]
  Componente1 = Arduino Uno (Rev3) - ICSP
  LED1 = LED - 5mm [color="Red (633nm)" package="5 mm [THT]"]  # not connected
  LED2 = LED - 5mm [color="Yellow (585nm)" package="5 mm [THT]"]
  LED3 = LED - 5mm [color="Green (555nm)" package="5 mm [THT]"]
  R2 = Resistor [tolerance=±5% resistance=470 package=THT]
  R3 = Resistor [tolerance=±5% resistance=470 package=THT]
  R4 = Resistor [tolerance=±5% resistance=470 package=THT]
  LED4 = LEDs [package=led10mm]

nets:
  N1: KY-1.signal, e-radionica_com1.VCC
  N2: KY-1.power, LED2.cathode, LED3.cathode
  N3: KY-1.ground, Componente1.D3_PWM
  N4: KY-1.C, LED4.A
  N5: e-radionica_com1.AO, Componente1.A5/SCL
  N6: Componente1.D6_PWM, R2.Pin_0
  N7: Componente1.D7, R4.Pin_0
  N8: LED2.anode, R2.Pin_1
  N9: LED3.anode, R3.Pin_1

custom parts:
  Keyes Relay: The Keyes 5V relay module is suitable for SCM development, home appliance control. It uses a 5V~12V TIL control signal which can control DC / AC signal.
  LEDs: LEDs Standard schematic elements and footprints for 5mm, 3mm, 1206, and 0603 sized LEDs. 5mm - Spark Fun Electronics SKU : COM-00529 (and others)
